# Fritzing sketch halloween-pumpkin-eyes (saved by Fritzing 0.9.3b)
breadboards: 1

parts:
  S2 = Basic Servo
  S3 = Basic Servo
  S4 = Basic Servo
  S5 = Basic Servo
  S6 = Basic Servo
  S7 = Basic Servo
  S8 = Basic Servo
  S9 = Basic Servo
  S10 = Basic Servo
  WeMos_D1_Mini1 = WeMos D1 Mini
  BATT1 = 4xAA Switchable Battery Pack w/Bare Wire
  S1 = Basic Servo

nets:
  GND: S2.gnd, S3.gnd, S5.gnd, S6.gnd, S7.gnd, S8.gnd, S9.gnd, S10.gnd, WeMos_D1_Mini1.G, BATT1.NEG, S1.gnd
  VCC: S2.vcc, S3.vcc, S5.vcc, S6.vcc, S7.vcc, S8.vcc, S9.vcc, S10.vcc, BATT1.POS, S1.vcc
  N1: S2.pulse, WeMos_D1_Mini1.D1
  N2: S3.pulse, WeMos_D1_Mini1.D2
  N3: S4.pulse, WeMos_D1_Mini1.D3
  N4: S5.pulse, WeMos_D1_Mini1.D4
  N5: S6.pulse, WeMos_D1_Mini1.D0
  N6: S7.pulse, WeMos_D1_Mini1.D5
  N7: S8.pulse, WeMos_D1_Mini1.D6
  N8: S9.pulse, WeMos_D1_Mini1.D7
  N9: S10.pulse, WeMos_D1_Mini1.D8
  N10: WeMos_D1_Mini1.TX, S1.pulse

custom parts:
  WeMos D1 Mini: The D1 mini is a mini wifi board based on ESP-8266EX.
  4xAA Switchable Battery Pack w/Bare Wire: 4xAA Switchable Battery Pack with Bare Wire connection
